# Fritzing sketch LED (saved by Fritzing 0.9.3b)
breadboards: 1

parts:
  부품1 = Arduino Uno (Rev3) - ICSP
  R1 = Resistor [tolerance=±5% resistance=220 package="0805 [SMD]"]
  LED1 = smd LED [color="Red (633nm)" package="0603 [SMD]"]

nets:
  N1: 부품1.D13/SCK, LED1.anode
  N2: 부품1.GND, R1.Pin_0
  N3: R1.Pin_1, LED1.cathode
