# Fritzing sketch PiezoBuzzer (saved by Fritzing 0.9.3b)
breadboards: 1

parts:
  부품1 = Arduino Uno (Rev3) - ICSP
  Piezo1 = Piezo Speaker - PC Mount [part_number=COM-07950]

nets:
  N1: 부품1.D8, Piezo1.VCC
  GND: 부품1.GND, Piezo1.GND

custom parts:
  Piezo Speaker - PC Mount: This is a small 12mm round speaker that operates around the audible 2kHz range. You can use these speakers to create simple music or user interfaces. Each speaker is PTH solderable and requires an operating voltage of 3.5-5V with a mean current of 35mA max. These speakers also have a typical sound output of 95 dBA and a coil resistance of 42 ±6.3 ohms.
