# Fritzing sketch Button (saved by Fritzing 0.9.3b)
breadboards: 1

parts:
  부품1 = Arduino Uno (Rev3) - ICSP
  LED1 = smd LED [color="Red (633nm)" package="0603 [SMD]"]
  R1 = Resistor [tolerance=±5% resistance=220 package="0805 [SMD]"]
  S1 = Momentary Switch [package=ksa_sealed_tac_switch]
  R2 = Resistor [tolerance=±5% resistance=220 package="0805 [SMD]"]

nets:
  N1: 부품1.D13/SCK, LED1.anode
  N2: 부품1.D2, S1.4, R2.Pin_1
  N3: 부품1.5V, S1.2
  N4: 부품1.GND, R1.Pin_0, R2.Pin_0
