# Fritzing sketch servomotor (saved by Fritzing 0.9.3b)

parts:
  부품1 = Arduino Uno (Rev3) - ICSP
  S1 = H-Bridge with L298N
  M1 = DC Motor
  M2 = DC Motor
  VCC1 = 4 x AAA Battery Mount
  VCC2 = 4 x AAA Battery Mount  # not connected

nets:
  N1: 부품1.D3_PWM, S1.IN4
  N2: 부품1.D4, S1.IN3
  N3: 부품1.D6_PWM, S1.IN2
  N4: 부품1.D7, S1.IN1
  GND: 부품1.GND, S1.GND, VCC1.-
  VIN: 부품1.VIN, S1.5V
  N5: S1.12V, VCC1.+
  N6: S1.M1-01, M2.pin_2
  N7: S1.M1-02, M2.pin_1
  N8: S1.M2-01, M1.pin_2
  N9: S1.M2-02, M1.pin_1

custom parts:
  H-Bridge with L298N: h-bridge
