# Fritzing sketch lightSensor (saved by Fritzing 0.9.3b)
breadboards: 1

parts:
  부품1 = Arduino Uno (Rev3) - ICSP
  R1 = Resistor [tolerance=±5% resistance=220 package="0805 [SMD]"]
  R2 = PHOTOCELL [package=photocell-kit]
  LED1 = smd LED [color="Red (633nm)" package="0603 [SMD]"]
  R3 = Resistor [tolerance=±5% resistance=220 package="0805 [SMD]"]

nets:
  N1: 부품1.A0, R1.Pin_1, R2.P$2
  N2: 부품1.D6_PWM, LED1.anode
  N3: 부품1.GND, R1.Pin_0, R2.P$1, R3.Pin_0
  N4: LED1.cathode, R3.Pin_1
