# Fritzing sketch lcd1602 (saved by Fritzing 0.9.3b)

parts:
  부품1 = Arduino Uno (Rev3) - ICSP
  LCD1 = LCD screen  # not connected
  LCM1602_IIC1 = LCM1602 IIC [part_number="LCM1602 IIC" chip_label="LCM1602 IIC" package="DIP (Dual Inline) [THT]"]

nets:
  N1: 부품1.A4/SDA, LCM1602_IIC1.SDA
  N2: 부품1.A5/SCL, LCM1602_IIC1.SCL
  GND: 부품1.GND, LCM1602_IIC1.GND
  5V: 부품1.5V, LCM1602_IIC1.VCC

custom parts:
  LCM1602 IIC: I2C-Module to use a 1602 or 2004 LCD on with the wire.h libory Serial LCD Modul
