# Fritzing sketch dht11 (saved by Fritzing 0.9.3b)
breadboards: 1

parts:
  부품1 = Arduino Uno (Rev3) - ICSP
  DHT1 = DHT11 Humitidy and Temperature Sensor
  R1 = Resistor [tolerance=±5% resistance=220 package="0805 [SMD]"]

nets:
  N1: 부품1.D4, DHT1.DATA, R1.Pin_1
  5V: 부품1.5V, DHT1.VDD
  GND: 부품1.GND, DHT1.GND, R1.Pin_0

custom parts:
  DHT11 Humitidy and Temperature Sensor: DHT11 Humidity and Temperature Sensor
