# Fritzing sketch bluetooth (saved by Fritzing 0.9.3b)
breadboards: 1

parts:
  부품1 = Arduino Uno (Rev3) - ICSP
  BT1 = Bluetooth HC-06u [package=THT]
  LED1 = smd LED [color="Red (633nm)" package="0603 [SMD]"]
  R1 = Resistor [tolerance=±5% resistance=220 package="0805 [SMD]"]

nets:
  N1: 부품1.D13/SCK, LED1.anode
  N2: 부품1.D2, BT1.RXD
  N3: 부품1.D3_PWM, BT1.TXD
  5V: 부품1.5V, BT1.VCC
  GND: 부품1.GND, BT1.GND, R1.Pin_0
  N4: LED1.cathode, R1.Pin_1

custom parts:
  Bluetooth HC-06u: Bluetooth HC-06 - face up, pins down 16.5mm x 37.5mm PCB
